// Logisim project ADDERS-circuit.circ as structural Verilog: 1 circuit, main circuit main
module main (
  input  in_1,
  input  in_2,
  input  in_3,
  input  in_4,
  input  in_5,
  output out_6,
  output out_7,
  output out_8,
  output out_9
);

  wire transistor_1_out, transistor_4_out, transistor_10_out, transistor_13_out, transistor_14_out,
       transistor_16_out, transistor_17_out, transistor_18_out, transistor_19_out, transistor_20_out,
       transistor_23_out, transistor_26_out, transistor_33_out, transistor_36_out, transistor_44_out,
       transistor_45_out;

  Transistor transistor_1 (.in(1'b1), .out(transistor_1_out), .gate(in_1));
  Transistor #(.\type ("n")) transistor_2 (.in(transistor_1_out), .out(out_6), .gate(in_3));
  Transistor #(.\type ("n")) transistor_3 (.in(transistor_4_out), .out(out_6), .gate(in_1));
  Transistor transistor_4 (.in(1'b0), .out(transistor_4_out), .gate(in_1));
  Transistor transistor_5 (.in(1'b1), .out(transistor_1_out), .gate(in_3));
  Transistor #(.\type ("n")) transistor_6 (.in(transistor_1_out), .out(out_6), .gate(in_1));
  Transistor transistor_7 (.in(transistor_4_out), .out(out_6), .gate(in_3));
  Transistor #(.\type ("n")) transistor_8 (.in(1'b0), .out(transistor_4_out), .gate(in_3));
  Transistor transistor_9 (.in(1'b0), .out(out_8), .gate(in_1));
  LED led_1 (.in(out_6));
  Transistor #(.\type ("n")) transistor_10 (.in(1'b1), .out(transistor_10_out), .gate(in_1));
  Transistor #(.\type ("n")) transistor_11 (.in(transistor_10_out), .out(out_8), .gate(in_3));
  LED led_2 (.in(out_8));
  Transistor transistor_12 (.in(1'b0), .out(out_8), .gate(in_3));
  Transistor transistor_13 (.in(1'b1), .out(transistor_13_out), .gate(in_2));
  Transistor #(.\type ("n")) transistor_14 (.in(transistor_13_out), .out(transistor_14_out), .gate(in_4));
  Transistor #(.\type ("n")) transistor_15 (.in(transistor_16_out), .out(transistor_14_out), .gate(in_2));
  Transistor transistor_16 (.in(1'b0), .out(transistor_16_out), .gate(in_2));
  Transistor transistor_17 (.in(1'b0), .out(transistor_17_out), .gate(in_2));
  Transistor transistor_18 (.in(1'b0), .out(transistor_18_out), .gate(in_2));
  Transistor transistor_19 (.in(1'b0), .out(transistor_19_out), .gate(in_5));
  Transistor #(.\type ("n")) transistor_20 (.in(1'b1), .out(transistor_20_out), .gate(in_2));
  Transistor #(.\type ("n")) transistor_21 (.in(transistor_20_out), .out(transistor_17_out), .gate(in_5));
  Transistor transistor_22 (.in(1'b0), .out(transistor_17_out), .gate(in_5));
  Transistor #(.\type ("n")) transistor_23 (.in(1'b1), .out(transistor_23_out), .gate(in_2));
  Transistor #(.\type ("n")) transistor_24 (.in(transistor_23_out), .out(transistor_18_out), .gate(in_4));
  Transistor transistor_25 (.in(1'b0), .out(transistor_18_out), .gate(in_4));
  Transistor #(.\type ("n")) transistor_26 (.in(1'b1), .out(transistor_26_out), .gate(in_5));
  Transistor #(.\type ("n")) transistor_27 (.in(transistor_26_out), .out(transistor_19_out), .gate(in_4));
  Transistor transistor_28 (.in(1'b0), .out(transistor_19_out), .gate(in_4));
  Transistor transistor_29 (.in(1'b1), .out(transistor_13_out), .gate(in_4));
  Transistor #(.\type ("n")) transistor_30 (.in(transistor_13_out), .out(transistor_14_out), .gate(in_2));
  Transistor transistor_31 (.in(transistor_16_out), .out(transistor_14_out), .gate(in_4));
  Transistor #(.\type ("n")) transistor_32 (.in(1'b0), .out(transistor_16_out), .gate(in_4));
  Transistor transistor_33 (.in(1'b1), .out(transistor_33_out), .gate(transistor_14_out));
  Transistor #(.\type ("n")) transistor_34 (.in(transistor_33_out), .out(out_7), .gate(in_5));
  Transistor #(.\type ("n")) transistor_35 (.in(transistor_36_out), .out(out_7), .gate(transistor_14_out));
  Transistor transistor_36 (.in(1'b0), .out(transistor_36_out), .gate(transistor_14_out));
  Transistor #(.\type ("n")) transistor_37 (.in(1'b1), .out(out_9), .gate(transistor_17_out));
  Transistor #(.\type ("n")) transistor_38 (.in(1'b1), .out(out_9), .gate(transistor_18_out));
  Transistor transistor_39 (.in(1'b1), .out(transistor_33_out), .gate(in_5));
  Transistor #(.\type ("n")) transistor_40 (.in(transistor_33_out), .out(out_7), .gate(transistor_14_out));
  Transistor transistor_41 (.in(transistor_36_out), .out(out_7), .gate(in_5));
  Transistor #(.\type ("n")) transistor_42 (.in(1'b0), .out(transistor_36_out), .gate(in_5));
  Transistor transistor_43 (.in(transistor_44_out), .out(out_9), .gate(transistor_17_out));
  Transistor transistor_44 (.in(transistor_45_out), .out(transistor_44_out), .gate(transistor_18_out));
  Transistor transistor_45 (.in(1'b0), .out(transistor_45_out), .gate(transistor_19_out));
  Transistor #(.\type ("n")) transistor_46 (.in(1'b1), .out(out_9), .gate(transistor_19_out));
  LED led_3 (.in(out_9));
  LED led_4 (.in(out_7));

  // Notes on the sheet:
  //   HALF ADDER
  //   FULL ADDER
endmodule
