// Logisim project ADDERS-logic.circ as structural Verilog: 1 circuit, main circuit main
module main (
  input  in_1,
  input  in_2,
  input  in_3,
  input  in_4,
  input  in_5,
  output out_6,
  output out_7,
  output out_8,
  output out_9
);

  wire and_2_out, and_3_out, and_4_out, xor_2_out;

  xor xor_1 (out_7, in_3, in_5);
  and and_1 (out_9, in_5, in_3);
  LED led_1 (.in(out_7));
  LED led_2 (.in(out_9));
  xor xor_2 (xor_2_out, in_1, in_2);
  and and_2 (and_2_out, in_1, in_2);
  and and_3 (and_3_out, in_1, in_4);
  and and_4 (and_4_out, in_2, in_4);
  xor xor_3 (out_6, xor_2_out, in_4);
  LED led_3 (.in(out_6));
  or or_1 (out_8, and_2_out, and_3_out, and_4_out);
  LED led_4 (.in(out_8));

  // Notes on the sheet:
  //   HALF ADDER
  //   FULL ADDER
endmodule
