// Logisim project Automatic-logics.circ as structural Verilog: 6 circuits, main circuit main
module main (
  input  in_1,
  input  [7:0] in_2,
  input  [7:0] in_3,
  output [7:0] out_4,
  output out_5
);

  Adder adder_1 (.a(in_3), .b(out_4), .out(in_2), .cin(in_1), .cout(out_5));
  Full_adder full_adder_1 ();  // open: A, B, C, D, S, C_2
endmodule

module Condicional (
  input  A,
  input  B,
  output S
);

  wire not_1_out;

  not not_1 (not_1_out, A);
  or or_1 (S, not_1_out, B);
endmodule

module Bicondicional (
  input  A,
  input  B,
  output S
);

  wire and_1_out, and_2_out, not_1_out, not_2_out;

  not not_1 (not_1_out, A);
  not not_2 (not_2_out, B);
  and and_1 (and_1_out, not_1_out, not_2_out);
  and and_2 (and_2_out, A, B);
  or or_1 (S, and_1_out, and_2_out);
endmodule

module XOR (
  input  A,
  input  B,
  output S
);

  wire and_1_out, and_2_out, not_1_out, not_2_out;

  not not_1 (not_1_out, A);
  not not_2 (not_2_out, B);
  and and_1 (and_1_out, not_1_out, B);
  and and_2 (and_2_out, A, not_2_out);
  or or_1 (S, and_1_out, and_2_out);
endmodule

module Half_adder (
  input  A,
  input  B,
  output S,
  output C
);

  wire nand_1_out, nand_2_out, nand_3_out, nand_4_out, nand_5_out;

  nand nand_1 (nand_1_out, A, A);
  nand nand_2 (nand_2_out, B, B);
  nand nand_3 (nand_3_out, A, B);
  nand nand_4 (nand_4_out, nand_1_out, B);
  nand nand_5 (nand_5_out, A, nand_2_out);
  nand nand_6 (C, nand_3_out, nand_3_out);
  nand nand_7 (S, nand_4_out, nand_5_out);
endmodule

module Full_adder (
  input  A,
  input  B,
  input  C,
  input  D,
  output S,
  output C_2
);

  wire and_1_out, and_2_out, and_3_out, and_4_out, and_5_out, and_6_out, and_7_out, and_8_out, and_9_out,
       and_10_out, and_11_out, and_12_out, and_13_out, and_14_out, not_1_out, not_2_out, not_3_out,
       not_4_out, not_5_out, not_6_out, not_7_out, not_8_out, not_9_out, not_10_out, not_11_out, not_12_out,
       not_13_out, not_14_out, not_15_out, not_16_out;

  not not_1 (not_1_out, A);
  not not_2 (not_2_out, B);
  not not_3 (not_3_out, C);
  not not_4 (not_4_out, A);
  not not_5 (not_5_out, B);
  not not_6 (not_6_out, D);
  not not_7 (not_7_out, A);
  not not_8 (not_8_out, C);
  not not_9 (not_9_out, D);
  not not_10 (not_10_out, A);
  not not_11 (not_11_out, B);
  not not_12 (not_12_out, C);
  not not_13 (not_13_out, D);
  not not_14 (not_14_out, B);
  not not_15 (not_15_out, C);
  not not_16 (not_16_out, D);
  and and_1 (and_1_out, C, D);
  and and_2 (and_2_out, B, D);
  and and_3 (and_3_out, B, C);
  and and_4 (and_4_out, A, D);
  and and_5 (and_5_out, A, C);
  and and_6 (and_6_out, A, B);
  and and_7 (and_7_out, not_1_out, not_2_out, not_3_out, D);
  and and_8 (and_8_out, not_4_out, not_5_out, C, not_6_out);
  and and_9 (and_9_out, not_7_out, B, not_8_out, not_9_out);
  and and_10 (and_10_out, not_10_out, B, C, D);
  and and_11 (and_11_out, A, not_11_out, not_12_out, not_13_out);
  and and_12 (and_12_out, A, not_14_out, C, D);
  and and_13 (and_13_out, A, B, not_15_out, D);
  and and_14 (and_14_out, A, B, C, not_16_out);
  or or_1 (C_2, and_1_out, and_2_out, and_3_out, and_4_out, and_5_out, and_6_out);
  or or_2 (S, and_7_out, and_8_out, and_9_out, and_10_out, and_11_out, and_12_out, and_13_out, and_14_out);
endmodule
