// Logisim project Display7-12char-logic.circ as structural Verilog
module main (
  input  _0,
  input  _1,
  input  _2,
  input  _3,
  input  _4,
  input  _5,
  input  _6,
  input  _7,
  input  _8,
  input  _9,
  input  A,
  input  B
);

  wire display_12char_1_a, display_12char_1_b, display_12char_1_c, display_12char_1_d, display_12char_1_e,
       display_12char_1_f, display_12char_1_g, display_12char_1_pt;

  Display_12char display_12char_1 (
    .B0(_0), .B1(_1), .B2(_2), .B3(_3), .B4(_4), .B5(_5), .B6(_6), .B7(_7), .B8(_8), .B9(_9), .Ba(A), .Bb(B),
    .A(display_12char_1_a), .B(display_12char_1_b), .C(display_12char_1_c), .D(display_12char_1_d),
    .E(display_12char_1_e), .F(display_12char_1_f), .G(display_12char_1_g), .PT(display_12char_1_pt));
  _7_Segment_Display u_7_segment_display_1 (
    .g(display_12char_1_g), .f(display_12char_1_f), .a(display_12char_1_a), .b(display_12char_1_b),
    .e(display_12char_1_e), .d(display_12char_1_d), .c(display_12char_1_c), .dp(display_12char_1_pt));
endmodule
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