// Logisim project NOT-circuit.circ as structural Verilog: 1 circuit, main circuit main
module main (
  input  in_1,
  input  in_2,
  input  in_3,
  output out_4,
  output out_5,
  output out_6
);

  Pull_Resistor #(.pull(1)) pull_resistor_1 (.node(out_6));
  Transistor #(.\type ("n")) transistor_1 (.in(1'b0), .out(out_6), .gate(in_3));
  LED led_1 (.in(out_6));
  Transistor transistor_2 (.in(1'b1), .out(out_4), .gate(in_2));
  LED led_2 (.in(out_4));
  Pull_Resistor pull_resistor_2 (.node(out_4));
  Transistor transistor_3 (.in(1'b1), .out(out_5), .gate(in_1));
  Transistor #(.\type ("n")) transistor_4 (.in(1'b0), .out(out_5), .gate(in_1));
  LED led_3 (.in(out_5));

  // Notes on the sheet:
  //   NOT
endmodule
